# Fritzing sketch doc1 (saved by Fritzing 0.8.7b)
circuit board: 8.46667cm x 5.64444cm
breadboards: 1

parts:
  R1 = Resistor [tolerance=±5% resistance=4.7k package=THT]
  R2 = Resistor [tolerance=±5% resistance=4.7k package=THT]
  R3 = Resistor [tolerance=±5% resistance=4.7k package=THT]
  R4 = Resistor [tolerance=±5% resistance=4.7k package=THT]
  P1 = S1133 Si Photodiode [package="8mm Ceramic [THT]"]
  P2 = S1133 Si Photodiode [package="8mm Ceramic [THT]"]
  P3 = S1133 Si Photodiode [package="8mm Ceramic [THT]"]
  P4 = S1133 Si Photodiode [package="8mm Ceramic [THT]"]
  Part2 = Arduino Nano (Rev3.0)
  M1 = Stepper Motor - Bipolar  # not connected
  M2 = Stepper Motor - Bipolar  # not connected

nets:
  N1: R1.Pin_0, P3.cathode
  N2: R1.Pin_1, R2.Pin_1, R3.Pin_1, R4.Pin_1, P1.anode, P2.anode, P3.anode, P4.anode, Part2.GND, Part2.A3, Part2.A2, Part2.A1, Part2.A0
  N3: R2.Pin_0, P2.cathode
  N4: R3.Pin_0, P4.cathode
  N5: R4.Pin_0, P1.cathode
